# Fritzing sketch Diagrama (saved by Fritzing 0.9.3b)
breadboards: 1

parts:
  Componente1 = Arduino Uno (Rev3)
  hc-sr1 = hc-sr04
  J1 = Piezo Speaker

nets:
  N1: Componente1.D2, J1.pin2
  N2: Componente1.D6_PWM, hc-sr1.Echo
  N3: Componente1.D7, hc-sr1.Trig
  5V: Componente1.5V, hc-sr1.VCC
  GND: Componente1.GND, hc-sr1.GND, J1.pin1
